# Fritzing sketch temp_humid_sender_wiring_diagram (saved by Fritzing 0.9.3b)
breadboards: 1

parts:
  Part1 = Itsy Bitsy 32u4 3V @ 8MHz [part_number="Adafruit 3675"]
  J1 = female pin header, 8 pins [form="♀ (female)" part_number="8 pin header"]
  Part4 = Adafruit Micro USB Breakout [part_number="Adafruit #1833"]
  J13 = female pin header, 8 pins [form="♀ (female)"]
  J14 = female pin header, 11 pins [form="♀ (female)"]
  J15 = female pin header, 4 pins [form="♀ (female)"]

nets:
  GND: Part1.GND, J1.pin1, Part4.GND, J15.pin4
  N1: Part1.VBUS, Part4.VBUS
  N2: Part1.D10, J1.pin5
  N3: Part1.D9, J1.pin3
  N4: Part1.D7, J1.pin4
  N5: Part1.SCL, J15.pin1
  N6: Part1.SDA, J15.pin2
  N7: Part1.MOSI, J1.pin6
  N8: Part1.SCK, J1.pin7
  N9: Part1.+3V3, J1.pin2, J1.pin8, J15.pin3
  N10: J13.pin1, J14.pin3
  N11: J13.pin2, J14.pin1
  N12: J13.pin3, J14.pin8
  N13: J13.pin4, J14.pin9
  N14: J13.pin5, J14.pin7
  N15: J13.pin6, J14.pin6
  N16: J13.pin7, J14.pin4
  N17: J13.pin8, J14.pin11

notes:
  TFT (back)
  (Vin) ... (lite)
  Standard 8 pin header connections (for TFT)
  Black: Ground
  Red: Vcc 3-5 ok
  Blue: Reset (gnd = reset) (Itsy D9)
  Green: D/C (data/command) (Itsy D7)
  Yellow: TFT CS (Itsy D10)
  White: MOSI (master out Slave In) (MOSI)
  Orange: SCLK (SPI clock) (SCK)
  Red: Lite (power 3-5 v)
  Micro USB Breakout
  (for power only)
  I2C (to sensor board)
  SCL - SDA - 3v - GND

custom parts:
  Itsy Bitsy 32u4 3V @ 8MHz: What's smaller than a Feather but larger than a Trinket? It's an Itsy Bitsy! Small, powerful, Arduino-compatible - this microcontroller board is perfect when you want something very compact, but still with a bunch of pins. Itsy Bitsy is only 1.4" long by 0.7" wide, but has 6 power pins, 6 analog & digital pins and 17 digital pins. It packs much of the same capability as an Arduino UNO or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
  Adafruit Micro USB Breakout: Simple but effective - this breakout board has a USB Micro-B connector, with all 5 pins broken out. Great for pairing with a microcontroller with USB support, or adding USB 5V power to a project. We use a micro-AB connector with through-hole shielding pads for an excellent strong connection - it won't rip off by accident! Comes with one fully assembled and tested micro B breakout PCB and a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
